# Fritzing sketch Capstone (saved by Fritzing 0.9.4)
breadboards: 1

parts:
  Argon1 = Particle Argon  # not connected
  S1 = Pushbutton [package="[THT]"]
  MAX30102_Sensor1 = MAX30102 Oximeter and Heart-Rate Sensor [part_number=MAX30102]  # not connected
  M1 = BMP280  # not connected

nets:
  N1: S1.Pin_3, S1.Pin_4

custom parts:
  Particle Argon: The Argon is a powerful Wi-Fi enabled development board that can act as either a standalone Wi-Fi endpoint or Wi-Fi enabled gateway for Particle Mesh networks. It is based on the Nordic nRF52840 and has built-in battery charging circuitry so it’s easy to connect a Li-Po and deploy your local network in minutes. The Argon is great for connecting existing projects to the Particle Device Cloud or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
  Pushbutton: A generic pushbutton.
  MAX30102 Oximeter and Heart-Rate Sensor: The MAX30102 is an integrated pulse oximetry and heart-rate monitor biosensor module. It includes internal LEDs, photodetectors, optical elements, and low-noise electronics with ambient light rejection. The MAX30102 operates on a single 1.8V power supply and a separate 3.3V power supply for the internal LEDs. Communication is through a I2C-compatible interface.
  BMP280: Temperature Humidity Barometric presure Sensor, I2C
